# Fritzing sketch layout amp2 (saved by Fritzing 0.9.3b)
perfboards: 1

parts:
  Q3 = NPN-Transistor [package="TO92 [THT]"]  # not connected
  Q4 = NPN-Transistor [package="TO92 [THT]"]  # not connected
  R9 = Resistor [tolerance=±5% resistance=220k package=THT]  # not connected
  R10 = Resistor [tolerance=±5% resistance=220k package=THT]
  Q7 = PNP-Transistor [package="TO92 [THT]"]
  Q11 = PNP-Transistor [package="TO92 [THT]"]
  R16 = Resistor [tolerance=±5% resistance=820 package=THT]  # not connected
  R18 = Resistor [tolerance=±5% resistance=51 package=THT]  # not connected
  R19 = Resistor [tolerance=±5% resistance=1k package=THT]  # not connected
  LED1 = LED - 5mm [color="Red (633nm)" package="5 mm [THT]"]  # not connected
  R23 = Resistor [tolerance=±5% resistance=1.5k package=THT]  # not connected
  R26 = Resistor [tolerance=±5% resistance=150 package=THT]  # not connected
  C5 = Ceramic Capacitor [capacitance=100nF package="100 mil [THT, multilayer]"]
  R29 = Resistor [tolerance=±5% resistance=51 package=THT]  # not connected
  C11 = Ceramic Capacitor [capacitance=100nF package="100 mil [THT, multilayer]"]  # not connected
  R39 = Resistor [tolerance=±5% resistance=8.2k package=THT]  # not connected
  Q19 = NPN-Transistor [package="TO92 [THT]"]  # not connected
  R40 = Resistor [tolerance=±5% resistance=47k package=THT]  # not connected
  R41 = Resistor [tolerance=±5% resistance=51 package=THT]  # not connected
  Q20 = NPN-Transistor [package="TO92 [THT]"]  # not connected
  R42 = Resistor [tolerance=±5% resistance=4.7k package=THT]  # not connected
  Q21 = NPN-Transistor [package="TO92 [THT]"]  # not connected
  Q22 = PNP-Transistor [package="TO92 [THT]"]  # not connected
  R43 = Resistor [tolerance=±5% resistance=22 package=THT]  # not connected
  LED2 = LED - 5mm [color="Red (633nm)" package="5 mm [THT]"]  # not connected
  R44 = Resistor [tolerance=±5% resistance=1.5k package=THT]  # not connected
  C12 = Ceramic Capacitor [capacitance=100nF package="100 mil [THT, multilayer]"]

nets:
  N1: R10.Pin_0, Q7.C, Q11.C
  N2: Q7.B, C5.1
  N3: Q11.B, C12.0
